# Fritzing sketch BoxLEDs (saved by Fritzing 0.9.3b)

parts:
  Часть1 = Arduino Mega 2560 (Rev3)
  Часть5 = MicroSD Card Module
  IC1 = DS1302 [package="DIP8 [THT]"]
  Часть7 = Matrix LED de 8x8 basada en MAX7219
  KEYPAD1 = Membrane Matrix Keypad
  KEYPAD2 = Membrane Matrix Keypad
  Часть8 = Adafruit MAX9814 Electret Microphone Amplifier [part_number="Adafruit #1713"]
  Часть9 = NeoPixel NeoMatrix 8x8 [part_number=1487]
  Часть11 = NeoPixel Jewel [part_number=2226]

nets:
  N1: Часть1.A0, Часть9.IN
  N2: Часть1.A1, Часть11.IN
  N3: Часть1.A2, IC1.Vbat_-_Backup_Supply
  N4: Часть1.A3, IC1.SCLK_-_SPI_Clock
  N5: Часть1.A4, IC1.I/O_-_SPI_Data_In/Out
  N6: Часть1.A7, Часть8.OUTPUT
  N7: Часть1.D13_PWM, Часть7.CLK
  N8: Часть1.D11_PWM, Часть7.DIN
  N9: Часть1.D10_PWM, Часть7.CS
  N10: Часть1.D22, KEYPAD1.1
  N11: Часть1.D23, KEYPAD1.2
  N12: Часть1.D24, KEYPAD1.3
  N13: Часть1.D25, KEYPAD1.4
  N14: Часть1.D26, KEYPAD1.5
  N15: Часть1.D27, KEYPAD1.6
  N16: Часть1.D28, KEYPAD1.7
  N17: Часть1.D30, KEYPAD2.1
  N18: Часть1.D31, KEYPAD2.2
  N19: Часть1.D32, KEYPAD2.3
  N20: Часть1.D33, KEYPAD2.4
  N21: Часть1.D34, KEYPAD2.5
  N22: Часть1.D35, Часть5.CS
  N23: Часть1.D50, Часть5.MISO
  N24: Часть1.D51, Часть5.MOSI
  N25: Часть1.D52, Часть5.SCK

custom parts:
  Membrane Matrix Keypad: Membrane Matrix 3x4 Keypad
  Adafruit MAX9814 Electret Microphone Amplifier: Add an ear to your project with this well-designed electret microphone amplifier with AGC. This fully assembled and tested board comes with a 20-20KHz electret microphone soldered on. For the amplification, we use the Maxim MAX9814, a specialty chip that is designed for amplifying electret microphones in situations where the loudness of the audio isn't predictable. This fancy microphone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
  NeoPixel NeoMatrix 8x8: Put on your sunglasses before wiring up this LED matrix - 64 eye-blistering RGB LEDs adorn the NeoMatrix for a blast of configurable color. Arranged in an 8x8 matrix, each pixel is individually addressable. Only one microcontroller pin is required to control all the LEDs, and you get 24 bit color for each LED.
  NeoPixel Jewel: We fit seven of our tiny 5050 (5mm x 5mm) smart RGB LEDs onto a beautiful, round PCB with mounting holes and a chainable design to create what we think is our most elegant (and evening-wear appropriate) NeoPixel board yet. Use only one microcontroller pin to control as many as you can chain together! Each LED is addressable as the driver chip is inside the LED. Each one has ~18mA constant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
